# Fritzing sketch FINAL-PROJECT (saved by Fritzing 0.8.7b)
breadboards: 1

parts:
  Part1 = Arduino Mega 2560 (Rev3)
  C1 = Capacitor [package=cap-pth-small2]
  R1 = Resistor [tolerance=±5% resistance=330 package=THT]
  R2 = Resistor [tolerance=±5% resistance=220 package=THT]

nets:
  N1: Part1.A0, C1.1, R1.Pin_1, R2.Pin_0
  N2: Part1.D13_PWM, R2.Pin_1
  N3: Part1.D11_PWM, R1.Pin_0
  N4: Part1.GND, C1.2
