# Fritzing sketch MIDTERM-PROJECT (saved by Fritzing 0.8.7b)
breadboards: 1

parts:
  Part1 = Arduino Mega 2560 (Rev3)
  R1 = Resistor [tolerance=±5% resistance=680 package=THT]
  R2 = Resistor [tolerance=±5% resistance=220 package=THT]
  R3 = Resistor [tolerance=±5% resistance=220 package=THT]
  R4 = Resistor [tolerance=±5% resistance=220 package=THT]

nets:
  N1: Part1.A8, R1.Pin_1, R2.Pin_0
  N2: Part1.A9, R2.Pin_1, R3.Pin_0
  N3: Part1.A10, R3.Pin_1, R4.Pin_0
  N4: Part1.GND, R1.Pin_0, R4.Pin_1
